// Digital circuit batalha-naval.dig as structural Verilog
module batalha_naval (
  input  Reset,
  input  clk,
  input  [3:0] in_4,
  input  in_6,
  output [2:0] out_3,
  output [5:0] out_5,
  output [3:0] out_7
);

  wire u_batalhaNaval_ganhou, u_batalhaNaval_perdeu;

  batalhaNaval #(.applicationType("GHDL"), .CodeFile("C:\\Users\\dreyr\\Desktop\\workspace\\BatalhaNaval\\batalhaNaval.vhdl")) u_batalhaNaval (
    .clock(clk), .reset(Reset), .entradas(in_4), .sentido(in_6), .naviosPosicionados(out_3), .vidas(out_5),
    .ganhou(u_batalhaNaval_ganhou), .perdeu(u_batalhaNaval_perdeu), .teste(out_7));
  LED led_1 (.in(u_batalhaNaval_ganhou));
  LED led_2 (.in(u_batalhaNaval_perdeu));
endmodule
